# Fritzing sketch MAIN draft 1.1 (saved by Fritzing 0.9.3b)

parts:
  Part1 = Arduino Mega 2560 (Rev3)-TopMount
  OLED_I2C1 = OLED 128x64 I2C Monochrome Display
  R1 = Resistor [tolerance=±5% resistance=10k package="0805 [SMD]"]
  S1 = Pushbutton [package="[SMD]"]
  R2 = Resistor [tolerance=±5% resistance=10k package="0805 [SMD]"]
  S2 = Pushbutton [package="[SMD]"]
  S3 = Pushbutton [package="[SMD]"]
  R3 = Resistor [tolerance=±5% resistance=10k package="0805 [SMD]"]

nets:
  N1: Part1.SCL, OLED_I2C1.SCK
  N2: Part1.SDA, OLED_I2C1.SDA
  5V: Part1.5V, OLED_I2C1.VDD, S1.Pin_3, S1.Pin_4, S2.Pin_3, S2.Pin_4
  GND: Part1.GND, OLED_I2C1.GND, R1.Pin_1, R2.Pin_1
  N3: Part1.D31, S3.Pin_1, S3.Pin_2, R3.Pin_0
  N4: Part1.D33, R2.Pin_0, S2.Pin_1, S2.Pin_2
  N5: Part1.D35, R1.Pin_0, S1.Pin_1, S1.Pin_2

notes:
  Register
  Delist
  Receive RF

custom parts:
  Arduino Mega 2560 (Rev3)-TopMount: Arduino Mega 2560 (Rev3) for Top PCB Mount. The PCB view of the Arduino Mega 2560 (Rev3) in Arduino Bin flipped upside down with the text flipped back so as to be readable. Other views haven't changed Protruding component position is outlined to provide indication of part contact. Number in component outline is mm of protrusion of the component from the Mega PCB. Subtract the number from the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
